# Fritzing sketch VendingMachine_Schematic (saved by Fritzing 0.9.3b)
breadboards: 1

parts:
  부품1 = Arduino Uno (Rev3) - ICSP
  hc-sr1 = hc-sr04
  hc-sr2 = hc-sr04
  hc-sr3 = hc-sr04
  J1 = Piezo Speaker
  J3 = Infrared Proximity Sensor
  S1 = Round Pushbutton
  J4 = Basic Servo
  VCC1 = 4 x AAA Battery Mount  # not connected

nets:
  N1: 부품1.A0, J3.Vout
  N2: 부품1.ICSP_MISO, 부품1.D12/MISO, S1.leg1
  N3: 부품1.ICSP_MOSI, 부품1.D11_PWM/MOSI, J4.pulse
  N4: 부품1.D8, hc-sr1.Echo
  N5: 부품1.D10_PWM/SS, J1.pin2
  N6: 부품1.D4, hc-sr3.Echo
  N7: 부품1.D5_PWM, hc-sr3.Trig
  N8: 부품1.D6_PWM, hc-sr2.Echo
  N9: 부품1.D7, hc-sr2.Trig
  5V: 부품1.5V, J3.Vcc
  GND: 부품1.GND, J3.GND
